# Fritzing sketch powerbox-wiring (saved by Fritzing 0.9.3b)

parts:
  U1 = NodeMCU V1.0
  U8 = Power Outlet [chip_label=IC package="SIP (Single Inline) [THT]"]
  U9 = Power Outlet [chip_label=IC package="SIP (Single Inline) [THT]"]
  U11 = Power Outlet [chip_label=IC package="SIP (Single Inline) [THT]"]
  U12 = 4-Channel 5v Relay Shield [package=relay-4ch5v10a]
  U13 = 4-Channel 5v Relay Shield [package=relay-4ch5v10a]
  U14 = Power Outlet [chip_label=IC package="SIP (Single Inline) [THT]"]

nets:
  N1: U1.D1, U12.IN1
  N2: U1.D2, U12.IN2
  VCC: U1.3V3, U12.VCC, U13.VCC
  GND: U1.GND, U12.GND, U13.GND
  N3: U1.D5, U12.IN3
  N4: U1.D6, U12.IN4
  N5: U1.D7, U13.IN1
  N6: U1.D8, U13.IN2
  N7: U1.RX, U13.IN3
  N8: U1.TX, U13.IN4
  N9: U8.hot1, U12.K4-Off
  N10: U8.hot2, U12.K3-Off
  N11: U8.neutral1, U8.neutral2, U9.neutral1, U9.neutral2, U11.neutral1, U11.neutral2, U14.neutral1, U14.neutral2
  N12: U8.ground, U9.ground, U11.ground, U14.ground
  N13: U9.hot1, U12.K2-Off
  N14: U9.hot2, U12.K1-Off
  N15: U11.hot1, U13.K2-Off
  N16: U11.hot2, U13.K1-Off
  N17: U12.K1-In, U12.K2-In, U12.K3-In, U12.K4-In, U13.K1-In, U13.K2-In, U13.K3-In, U13.K4-In
  N18: U13.K3-Off, U14.hot2
  N19: U13.K4-Off, U14.hot1

notes:
  To outlet

custom parts:
  NodeMCU V1.0: ESP8266 based NodeMCU
  Power Outlet: A standard power outlet. Silver screws are neutral, brass screws are hot. Green screw is ground.
  4-Channel 5v Relay Shield: 4 Channel 5v Relay Shield w. 2x SPD-06VDC-SD-C
